// Logisim project cpu.circ as structural Verilog: 2 circuits, main circuit main
module main (
  input  [31:0] INSTRUCTION,
  input  CLOCK,
  output [31:0] FETCH_ADDRESS,
  output [31:0] s0_Value,
  output [31:0] s1_Value,
  output [31:0] s2_Value,
  output [31:0] ra_Value,
  output [31:0] sp_Value
);

  wire ALUsrc, and_1_out, and_2_out, beq, bne, equal, jump, jumpreg, MemtoReg, MemWr, RegDst, RegWr;
  wire [3:0] ALUctr;
  wire [4:0] multiplexer_5_out;
  wire [15:0] IMM16;
  wire [25:0] IMM26;
  wire [31:0] adder_1_out, adder_2_out, bit_extender_1_out, bit_extender_2_out, bit_extender_3_out,
       main_1_read_data_2, main_2_result, main_3_p5, multiplexer_1_out, multiplexer_2_out, multiplexer_3_out,
       multiplexer_4_out, multiplexer_6_out, multiplexer_7_out, RS_value;

  assign bit_extender_1_out = {{16{1'b0}}, IMM16};  // Bit_Extender bit_extender_1
  Adder #(.width(32)) adder_1 (.a(FETCH_ADDRESS), .b(32'h4), .out(adder_1_out));  // open: cin, cout
  Adder #(.width(32)) adder_2 (.a(adder_1_out), .b(bit_extender_1_out), .out(adder_2_out));  // open: cin, cout
  Multiplexer #(.width(32), .enable("false")) multiplexer_1 (
    .in0(adder_1_out), .in1(adder_2_out), .out(multiplexer_1_out), .sel(and_1_out));
  and and_1 (and_1_out, beq, equal);
  Multiplexer #(.width(32), .enable("false")) multiplexer_2 (
    .in0(multiplexer_1_out), .in1(adder_2_out), .out(multiplexer_2_out), .sel(and_2_out));
  and and_2 (and_2_out, bne, ~equal);  // AND_Gate
  assign bit_extender_2_out = {{6{1'b0}}, IMM26};  // Bit_Extender bit_extender_2
  Multiplexer #(.width(32), .enable("false")) multiplexer_3 (
    .in0(multiplexer_2_out), .in1(bit_extender_2_out), .out(multiplexer_3_out), .sel(jump));
  Multiplexer #(.width(32), .enable("false")) multiplexer_4 (
    .in0(multiplexer_3_out), .in1(RS_value), .out(multiplexer_4_out), .sel(jumpreg));
  Register #(.width(32)) PC (.D(multiplexer_4_out), .Q(FETCH_ADDRESS), .clk(CLOCK));  // open: en, clr
  Multiplexer #(.width(5)) multiplexer_5 (
    .in0(INSTRUCTION[20:16]), .in1(INSTRUCTION[25:21]), .out(multiplexer_5_out), .sel(RegDst));  // open: en
  regfile_main main_1 (
    .Read_Register_1(INSTRUCTION[15:11]), .Read_Register_2(INSTRUCTION[20:16]),
    .Write_Register(multiplexer_5_out), .Write_Data(multiplexer_7_out), .Write_Enable(RegWr), .Clock(CLOCK),
    .Read_Data_1(RS_value), .Read_Data_2(main_1_read_data_2), .s0_Value(s0_Value), .s1_Value(s1_Value),
    .s2_Value(s2_Value), .ra_Value(ra_Value), .sp_Value(sp_Value));
  assign bit_extender_3_out = {{16{1'b0}}, IMM16};  // Bit_Extender bit_extender_3
  Multiplexer #(.width(32), .enable("false")) multiplexer_6 (
    .in0(main_1_read_data_2), .in1(bit_extender_3_out), .out(multiplexer_6_out), .sel(ALUsrc));
  alu_main main_2 (
    .Switch(ALUctr), .X(RS_value), .Equal(equal), .Result(main_2_result), .Y(multiplexer_6_out));  // open: Signed_Overflow
  // mem_main main_3: pin names not known; wires that end beside it: main_2_result, main_1_read_data_2, MemWr, CLOCK, main_3_p5
  Multiplexer #(.width(32), .enable("false")) multiplexer_7 (
    .in0(main_2_result), .in1(main_3_p5), .out(multiplexer_7_out), .sel(MemtoReg));

  // Other names for the same wires on the sheet: clk = CLOCK; fetch_addr[31:0] = FETCH_ADDRESS;
  //   RS[4:0] = INSTRUCTION[15:11]; RT[4:0] = INSTRUCTION[20:16]; RD[4:0] = INSTRUCTION[25:21]; ra[31:0] = ra_Value;
  //   s0[31:0] = s0_Value; s1[31:0] = s1_Value; s2[31:0] = s2_Value; sp[31:0] = sp_Value

  // Notes on the sheet:
  //   Output
  //   These are outputs/inputs from run.circ
  //   Inputs
  //   These are DEBUG/TEST outputs from your circuit.
endmodule

module controller_circ (
  input  [5:0] in_1,
  input  [5:0] in_2,
  input  [31:0] in_3,
  output RegDst,
  output RegWr,
  output ExtOp,
  output ALUsrc,
  output [3:0] ALUctr,
  output MemWr,
  output MemtoReg,
  output beq,
  output bne,
  output jump,
  output jumpreg
);

  wire isaddi, isaddiu, isandi, isbeq, isbne, isjal, isjump, isjumpreg, islw, isori, isrtype, isslti,
       issltiu, issw;

  and and_1 (isrtype, ~in_1[1], ~in_1[1], ~in_1[2], ~in_1[3], ~in_1[4], ~in_1[5]);  // AND_Gate
  and and_2 (isaddi, ~in_1[1], ~in_1[1], ~in_1[2], in_1[3], ~in_1[4], ~in_1[5]);  // AND_Gate
  and and_3 (isaddiu, in_1[1], ~in_1[1], ~in_1[2], in_1[3], ~in_1[4], ~in_1[5]);  // AND_Gate
  and and_4 (isandi, ~in_1[1], ~in_1[1], in_1[2], in_1[3], ~in_1[4], ~in_1[5]);  // AND_Gate
  and and_5 (isbeq, ~in_1[1], ~in_1[1], in_1[2], ~in_1[3], ~in_1[4], ~in_1[5]);  // AND_Gate
  and and_6 (isbne, in_1[1], ~in_1[1], in_1[2], ~in_1[3], ~in_1[4], ~in_1[5]);  // AND_Gate
  and and_7 (isjump, ~in_1[1], in_1[1], ~in_1[2], ~in_1[3], ~in_1[4], ~in_1[5]);  // AND_Gate
  and and_8 (isjal, in_1[1], in_1[1], ~in_1[2], ~in_1[3], ~in_1[4], ~in_1[5]);  // AND_Gate
  and and_9 (islw, in_1[1], in_1[1], ~in_1[2], ~in_1[3], ~in_1[4], in_1[5]);  // AND_Gate
  and and_10 (isori, in_1[1], ~in_1[1], in_1[2], in_1[3], ~in_1[4], ~in_1[5]);  // AND_Gate
  and and_11 (isslti, ~in_1[1], in_1[1], ~in_1[2], in_1[3], ~in_1[4], ~in_1[5]);  // AND_Gate
  and and_12 (issltiu, in_1[1], in_1[1], ~in_1[2], in_1[3], ~in_1[4], ~in_1[5]);  // AND_Gate
  and and_13 (issw, in_1[1], in_1[1], ~in_1[2], in_1[3], ~in_1[4], in_1[5]);  // AND_Gate
  buf or_1 (RegDst, isrtype);  // OR_Gate
  or or_2 (RegWr, isrtype, isaddi, isaddiu, isandi);
  or or_3 (ExtOp, isaddi, isaddiu);
  or or_4 (ALUsrc, isaddi, isaddiu, isandi);
  // OR_Gate or_5 has open pins: out=MemtoReg
  Multiplexer #(.select(5), .width(4)) multiplexer_1 (
    .in0(4'b0000), .in2(4'b0001), .in3(4'b0010), .in16(4'b0101), .in17(4'b0110), .in18(4'b0111),
    .in19(4'b1000), .in22(4'b1001), .in23(4'b1010), .in26(4'b1011), .in27(4'b1100), .out(ALUctr),
    .sel({in_2[5], in_2[3:0]}), .en(isrtype));  // open: in1, in4, in5, in6, in7, in8, in9, in10, in11, in12, in13, in14, in15, in20, in21, in24, in25, in28, in29, in30, in31
  buf or_6 (jump, isjump);  // OR_Gate
  buf or_7 (jumpreg, isjumpreg);  // OR_Gate
  buf or_8 (beq, isbeq);  // OR_Gate
  buf or_9 (bne, isbne);  // OR_Gate

  assign in_1[0] = in_1[1];
  assign in_3[20:11] = {in_3[25:21], in_3[25:21]};

  // Other names for the same wires on the sheet: funct[5:0] = in_2; funct1[5:0] = in_3[5:0];
  //   instruction[31:0] = {in_3[31:21], in_3[25:21], in_3[25:21], in_3[10:0]}; shamt[4:0] = in_3[10:6];
  //   rd[4:0] = in_3[25:21]; opcode1[5:0] = in_3[31:26]; opcode[5:0] = {in_1[5:1], in_1[1]}

  // Notes on the sheet:
  //   Determine the type of instruction:
  //   OUTPUTS
  //   for our ISA, the 4 bit of the funct code is always zero so get rid of it to use a 5bit MUX
endmodule
